# Fritzing sketch Read_scheme (saved by Fritzing 0.9.10b)
breadboards: 1

parts:
  Part1 = Adafruit T-Cobbler Plus [part_number="Adafruit #1989 and #2028"]
  LCM1602_IIC1 = LCM1602 IIC [part_number="LCM1602 IIC" chip_label="LCM1602 IIC" package="DIP (Dual Inline) [THT]"]
  LCD1 = LCD screen
  Part2 = RFID-RC522-v2
  LED1 = smd LED [color="Green (555nm)" package="0805 [SMD]"]
  LED2 = smd LED [color="Red (633nm)" package="0805 [SMD]"]
  R1 = Resistor [tolerance=±5% resistance=220 package="2512 [SMD]"]
  R2 = Resistor [tolerance=±5% resistance=220 package="2512 [SMD]"]
  8x8_LED_Modul_mit_MAX1 = 8x8 LED Modul mit MAX7219 [package=THT]

nets:
  +3.3V: Part1.+3.3V, Part2.3.3V
  N1: Part1.SDA, LCM1602_IIC1.SDA
  N2: Part1.SCL, LCM1602_IIC1.SCL
  GND: Part1.GND, LCM1602_IIC1.GND, Part2.GND, R1.Pin_1, R2.Pin_1, 8x8_LED_Modul_mit_MAX1.GND_Eingang
  N3: Part1.MOSI, Part2.MOSI
  N4: Part1.MISO, Part2.MISO
  N5: Part1.SCLK, Part2.SCK
  N6: Part1.GPIO13, LED1.anode
  N7: Part1.GPIO19, LED2.anode
  +5V: Part1.+5V, LCM1602_IIC1.VCC, 8x8_LED_Modul_mit_MAX1.VCC_Eingang
  N8: Part1.GPIO25, Part2.RST
  N9: Part1.CE0, Part2.SDA
  N10: Part1.GPIO16, 8x8_LED_Modul_mit_MAX1.CS_Eingang
  N11: Part1.GPIO20, 8x8_LED_Modul_mit_MAX1.DIN_Eingang
  N12: Part1.GPIO21, 8x8_LED_Modul_mit_MAX1.CLK_Eingang
  VSS: LCM1602_IIC1.VSS, LCD1.VSS
  VDD: LCM1602_IIC1.VDD, LCD1.VDD
  N13: LCM1602_IIC1.V0, LCD1.V0
  N14: LCM1602_IIC1.RS, LCD1.RS
  N15: LCM1602_IIC1.RW, LCD1.R/W
  N16: LCM1602_IIC1.E, LCD1.E
  N17: LCM1602_IIC1.D0, LCD1.DB0
  N18: LCM1602_IIC1.D1, LCD1.DB1
  N19: LCM1602_IIC1.D2, LCD1.DB2
  N20: LCM1602_IIC1.D3, LCD1.DB3
  N21: LCM1602_IIC1.D4, LCD1.DB4
  N22: LCM1602_IIC1.D5, LCD1.DB5
  N23: LCM1602_IIC1.D6, LCD1.DB6
  N24: LCM1602_IIC1.D7, LCD1.DB7
  N25: LCM1602_IIC1.A, LCD1.LED+
  N26: LCM1602_IIC1.K, LCD1.LED-
  N27: LED1.cathode, R2.Pin_0
  N28: LED2.cathode, R1.Pin_0

custom parts:
  Adafruit T-Cobbler Plus: The Raspberry Pi has landed on the Maker World like a 40-GPIO pinned, quad-USB ported, credit card sized bomb of DIY joy. And while you can use most of our great Model B accessories by hooking up our downgrade cable, its probably a good time to upgrade your set up and accessorize using all of the 40 pins. That's why we now carry the Assembled Adafruit Pi T-Cobbler Plus - Breakout + Cable for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
  LCM1602 IIC: I2C-Module to use a 1602 or 2004 LCD on with the wire.h libory Serial LCD Modul
  RFID-RC522-v2: A simple China made RFID-RC522 Reader; do check the pin labels, as this is a MFRC522 based clone.
